// Logisim project CPU_Design.circ as structural Verilog: 12 circuits, main circuit HalfComparator
module HalfComparator (
  input  A,
  input  B,
  output gt,
  output lt,
  output eq
);

  wire not_1_out, not_2_out;

  not not_1 (not_1_out, A);
  not not_2 (not_2_out, B);
  and and_1 (lt, B, not_1_out);
  and and_2 (gt, A, not_2_out);
  xnor xnor_1 (eq, B, A);
endmodule

module FullComparator (
  input  A,
  input  B,
  input  gt_in,
  input  lt_in,
  input  eq_in,
  output gt_out,
  output lt_out,
  output eq_out
);

  wire and_1_out, and_2_out, not_1_out, not_2_out, xnor_1_out;

  not not_1 (not_1_out, B);
  not not_2 (not_2_out, A);
  and and_1 (and_1_out, A, eq_in, not_1_out);
  and and_2 (and_2_out, B, not_2_out);
  xnor xnor_1 (xnor_1_out, B, A);
  or or_1 (gt_out, and_1_out, gt_in);
  and and_3 (eq_out, xnor_1_out, eq_in);
  or or_2 (lt_out, and_2_out, lt_in);
endmodule

module RegisterFile (
  input  [2:0] ReadRegister1,
  input  [2:0] ReadRegister2,
  input  [2:0] Write_Register,
  input  reset,
  input  Clock,
  input  [15:0] Input,
  input  RegisterWrite,
  output [15:0] ReadData1,
  output [15:0] ReadData2
);

  wire and_1_out, and_2_out, and_3_out, and_4_out, and_5_out, and_6_out, and_7_out, and_8_out,
       decoder_1_out0, decoder_1_out1, decoder_1_out2, decoder_1_out3, decoder_1_out4, decoder_1_out5,
       decoder_1_out6, decoder_1_out7;
  wire [15:0] register_1_q, register_2_q, register_3_q, register_4_q, register_5_q, register_6_q,
       register_7_q, register_8_q;

  Decoder #(.select(3)) decoder_1 (
    .out0(decoder_1_out0), .out1(decoder_1_out1), .out2(decoder_1_out2), .out3(decoder_1_out3),
    .out4(decoder_1_out4), .out5(decoder_1_out5), .out6(decoder_1_out6), .out7(decoder_1_out7),
    .sel(Write_Register));  // open: en
  and and_1 (and_1_out, decoder_1_out0, RegisterWrite);
  and and_2 (and_2_out, decoder_1_out1, RegisterWrite);
  and and_3 (and_3_out, decoder_1_out2, RegisterWrite);
  and and_4 (and_4_out, decoder_1_out3, RegisterWrite);
  and and_5 (and_5_out, decoder_1_out4, RegisterWrite);
  and and_6 (and_6_out, decoder_1_out5, RegisterWrite);
  and and_7 (and_7_out, decoder_1_out6, RegisterWrite);
  and and_8 (and_8_out, decoder_1_out7, RegisterWrite);
  Register #(.width(16)) register_1 (.D(Input), .en(and_1_out), .Q(register_1_q), .clk(Clock), .clr(reset));
  Register #(.width(16)) register_2 (.D(Input), .en(and_2_out), .Q(register_2_q), .clk(Clock), .clr(reset));
  Register #(.width(16)) register_3 (.D(Input), .en(and_3_out), .Q(register_3_q), .clk(Clock), .clr(reset));
  Register #(.width(16)) register_4 (.D(Input), .en(and_4_out), .Q(register_4_q), .clk(Clock), .clr(reset));
  Register #(.width(16)) register_5 (.D(Input), .en(and_5_out), .Q(register_5_q), .clk(Clock), .clr(reset));
  Register #(.width(16)) register_6 (.D(Input), .en(and_6_out), .Q(register_6_q), .clk(Clock), .clr(reset));
  Register #(.width(16)) register_7 (.D(Input), .en(and_7_out), .Q(register_7_q), .clk(Clock), .clr(reset));
  Register #(.width(16)) register_8 (.D(Input), .en(and_8_out), .Q(register_8_q), .clk(Clock), .clr(reset));
  Multiplexer #(.select(3), .width(16)) multiplexer_1 (
    .in0(register_1_q), .in1(register_2_q), .in2(register_3_q), .in3(register_4_q), .in4(register_5_q),
    .in5(register_6_q), .in6(register_7_q), .in7(register_8_q), .out(ReadData1), .sel(ReadRegister1));  // open: en
  Multiplexer #(.select(3), .width(16)) multiplexer_2 (
    .in0(register_1_q), .in1(register_2_q), .in2(register_3_q), .in3(register_4_q), .in4(register_5_q),
    .in5(register_6_q), .in6(register_7_q), .in7(register_8_q), .out(ReadData2), .sel(ReadRegister2));  // open: en
endmodule

module _16BitComparator (
  input  [15:0] A,
  input  [15:0] B,
  input  enable,
  output gt,
  output lt,
  output eq
);

  wire fullcomparator_1_eq_out, fullcomparator_1_gt_out, fullcomparator_1_lt_out, fullcomparator_2_eq_out,
       fullcomparator_2_gt_out, fullcomparator_2_lt_out, fullcomparator_3_eq_out, fullcomparator_3_gt_out,
       fullcomparator_3_lt_out, fullcomparator_4_eq_out, fullcomparator_4_gt_out, fullcomparator_4_lt_out,
       fullcomparator_5_eq_out, fullcomparator_5_gt_out, fullcomparator_5_lt_out, fullcomparator_6_eq_out,
       fullcomparator_6_gt_out, fullcomparator_6_lt_out, fullcomparator_7_eq_out, fullcomparator_7_gt_out,
       fullcomparator_7_lt_out, fullcomparator_8_eq_out, fullcomparator_8_gt_out, fullcomparator_8_lt_out,
       fullcomparator_9_eq_out, fullcomparator_9_gt_out, fullcomparator_9_lt_out, fullcomparator_10_eq_out,
       fullcomparator_10_gt_out, fullcomparator_10_lt_out, fullcomparator_11_eq_out,
       fullcomparator_11_gt_out, fullcomparator_11_lt_out, fullcomparator_12_eq_out,
       fullcomparator_12_gt_out, fullcomparator_12_lt_out, fullcomparator_13_eq_out,
       fullcomparator_13_gt_out, fullcomparator_13_lt_out, fullcomparator_14_eq_out,
       fullcomparator_14_gt_out, fullcomparator_14_lt_out, fullcomparator_15_eq_out,
       fullcomparator_15_gt_out, fullcomparator_15_lt_out, halfcomparator_1_eq, halfcomparator_1_gt,
       halfcomparator_1_lt;

  HalfComparator halfcomparator_1 (
    .A(A[15]), .B(B[15]), .gt(halfcomparator_1_gt), .lt(halfcomparator_1_lt), .eq(halfcomparator_1_eq));
  FullComparator fullcomparator_1 (
    .A(A[14]), .B(B[14]), .gt_in(halfcomparator_1_gt), .lt_in(halfcomparator_1_lt),
    .eq_in(halfcomparator_1_eq), .gt_out(fullcomparator_1_gt_out), .lt_out(fullcomparator_1_lt_out),
    .eq_out(fullcomparator_1_eq_out));
  FullComparator fullcomparator_2 (
    .A(A[4]), .B(B[4]), .gt_in(fullcomparator_14_gt_out), .lt_in(fullcomparator_14_lt_out),
    .eq_in(fullcomparator_14_eq_out), .gt_out(fullcomparator_2_gt_out), .lt_out(fullcomparator_2_lt_out),
    .eq_out(fullcomparator_2_eq_out));
  FullComparator fullcomparator_3 (
    .A(A[13]), .B(B[13]), .gt_in(fullcomparator_1_gt_out), .lt_in(fullcomparator_1_lt_out),
    .eq_in(fullcomparator_1_eq_out), .gt_out(fullcomparator_3_gt_out), .lt_out(fullcomparator_3_lt_out),
    .eq_out(fullcomparator_3_eq_out));
  FullComparator fullcomparator_4 (
    .A(A[3]), .B(B[3]), .gt_in(fullcomparator_2_gt_out), .lt_in(fullcomparator_2_lt_out),
    .eq_in(fullcomparator_2_eq_out), .gt_out(fullcomparator_4_gt_out), .lt_out(fullcomparator_4_lt_out),
    .eq_out(fullcomparator_4_eq_out));
  FullComparator fullcomparator_5 (
    .A(A[12]), .B(B[12]), .gt_in(fullcomparator_3_gt_out), .lt_in(fullcomparator_3_lt_out),
    .eq_in(fullcomparator_3_eq_out), .gt_out(fullcomparator_5_gt_out), .lt_out(fullcomparator_5_lt_out),
    .eq_out(fullcomparator_5_eq_out));
  FullComparator fullcomparator_6 (
    .A(A[2]), .B(B[2]), .gt_in(fullcomparator_4_gt_out), .lt_in(fullcomparator_4_lt_out),
    .eq_in(fullcomparator_4_eq_out), .gt_out(fullcomparator_6_gt_out), .lt_out(fullcomparator_6_lt_out),
    .eq_out(fullcomparator_6_eq_out));
  FullComparator fullcomparator_7 (
    .A(A[11]), .B(B[11]), .gt_in(fullcomparator_5_gt_out), .lt_in(fullcomparator_5_lt_out),
    .eq_in(fullcomparator_5_eq_out), .gt_out(fullcomparator_7_gt_out), .lt_out(fullcomparator_7_lt_out),
    .eq_out(fullcomparator_7_eq_out));
  FullComparator fullcomparator_8 (
    .A(A[1]), .B(B[1]), .gt_in(fullcomparator_6_gt_out), .lt_in(fullcomparator_6_lt_out),
    .eq_in(fullcomparator_6_eq_out), .gt_out(fullcomparator_8_gt_out), .lt_out(fullcomparator_8_lt_out),
    .eq_out(fullcomparator_8_eq_out));
  FullComparator fullcomparator_9 (
    .A(A[9]), .B(B[9]), .gt_in(fullcomparator_10_gt_out), .lt_in(fullcomparator_10_lt_out),
    .eq_in(fullcomparator_10_eq_out), .gt_out(fullcomparator_9_gt_out), .lt_out(fullcomparator_9_lt_out),
    .eq_out(fullcomparator_9_eq_out));
  FullComparator fullcomparator_10 (
    .A(A[10]), .B(B[10]), .gt_in(fullcomparator_7_gt_out), .lt_in(fullcomparator_7_lt_out),
    .eq_in(fullcomparator_7_eq_out), .gt_out(fullcomparator_10_gt_out), .lt_out(fullcomparator_10_lt_out),
    .eq_out(fullcomparator_10_eq_out));
  FullComparator fullcomparator_11 (
    .A(A[0]), .B(B[0]), .gt_in(fullcomparator_8_gt_out), .lt_in(fullcomparator_8_lt_out),
    .eq_in(fullcomparator_8_eq_out), .gt_out(fullcomparator_11_gt_out), .lt_out(fullcomparator_11_lt_out),
    .eq_out(fullcomparator_11_eq_out));
  FullComparator fullcomparator_12 (
    .A(A[8]), .B(B[8]), .gt_in(fullcomparator_9_gt_out), .lt_in(fullcomparator_9_lt_out),
    .eq_in(fullcomparator_9_eq_out), .gt_out(fullcomparator_12_gt_out), .lt_out(fullcomparator_12_lt_out),
    .eq_out(fullcomparator_12_eq_out));
  FullComparator fullcomparator_13 (
    .A(A[7]), .B(B[7]), .gt_in(fullcomparator_12_gt_out), .lt_in(fullcomparator_12_lt_out),
    .eq_in(fullcomparator_12_eq_out), .gt_out(fullcomparator_13_gt_out), .lt_out(fullcomparator_13_lt_out),
    .eq_out(fullcomparator_13_eq_out));
  assign eq = enable ? fullcomparator_11_eq_out : 1'bz;  // Controlled_Buffer controlled_buffer_1
  FullComparator fullcomparator_14 (
    .A(A[5]), .B(A[5]), .gt_in(fullcomparator_15_gt_out), .lt_in(fullcomparator_15_lt_out),
    .eq_in(fullcomparator_15_eq_out), .gt_out(fullcomparator_14_gt_out), .lt_out(fullcomparator_14_lt_out),
    .eq_out(fullcomparator_14_eq_out));
  FullComparator fullcomparator_15 (
    .A(A[6]), .B(B[6]), .gt_in(fullcomparator_13_gt_out), .lt_in(fullcomparator_13_lt_out),
    .eq_in(fullcomparator_13_eq_out), .gt_out(fullcomparator_15_gt_out), .lt_out(fullcomparator_15_lt_out),
    .eq_out(fullcomparator_15_eq_out));
  assign gt = enable ? fullcomparator_11_gt_out : 1'bz;  // Controlled_Buffer controlled_buffer_2
  assign lt = enable ? fullcomparator_11_lt_out : 1'bz;  // Controlled_Buffer controlled_buffer_3

  assign B[5] = A[5];
endmodule

module FullAdder (
  input  A,
  input  B,
  input  Carry_in,
  output Result,
  output Carry_out
);

  wire and_1_out, and_2_out, or_1_out;

  or or_1 (or_1_out, B, Carry_in);
  and and_1 (and_1_out, ~A, B, Carry_in);  // AND_Gate
  and and_2 (and_2_out, A, or_1_out);
  xor xor_1 (Result, A, B, Carry_in);
  or or_2 (Carry_out, and_1_out, and_2_out);
endmodule

module _16bitAdder (
  input  [15:0] A,
  input  [15:0] B,
  output [15:0] INST_Read,
  output c_out
);

  wire fulladder_1_carry_out, fulladder_2_carry_out, fulladder_3_carry_out, fulladder_4_carry_out,
       fulladder_5_carry_out, fulladder_6_carry_out, fulladder_7_carry_out, fulladder_8_carry_out,
       fulladder_9_carry_out, fulladder_10_carry_out, fulladder_11_carry_out, fulladder_12_carry_out,
       fulladder_13_carry_out, fulladder_14_carry_out, halfadder_1_carry_out;

  HalfAdder halfadder_1 (.A(B[0]), .B(A[0]), .Sum(INST_Read[0]), .carry_out(halfadder_1_carry_out));
  FullAdder fulladder_1 (
    .A(A[1]), .B(B[1]), .Carry_in(halfadder_1_carry_out), .Result(INST_Read[1]),
    .Carry_out(fulladder_1_carry_out));
  FullAdder fulladder_2 (
    .A(A[2]), .B(B[2]), .Carry_in(fulladder_1_carry_out), .Result(INST_Read[2]),
    .Carry_out(fulladder_2_carry_out));
  FullAdder fulladder_3 (
    .A(A[3]), .B(B[3]), .Carry_in(fulladder_2_carry_out), .Result(INST_Read[3]),
    .Carry_out(fulladder_3_carry_out));
  FullAdder fulladder_4 (
    .A(A[4]), .B(B[4]), .Carry_in(fulladder_3_carry_out), .Result(INST_Read[4]),
    .Carry_out(fulladder_4_carry_out));
  FullAdder fulladder_5 (
    .A(A[5]), .B(B[5]), .Carry_in(fulladder_4_carry_out), .Result(INST_Read[5]),
    .Carry_out(fulladder_5_carry_out));
  FullAdder fulladder_6 (
    .A(A[6]), .B(B[6]), .Carry_in(fulladder_5_carry_out), .Result(INST_Read[6]),
    .Carry_out(fulladder_6_carry_out));
  FullAdder fulladder_7 (
    .A(A[7]), .B(B[7]), .Carry_in(fulladder_6_carry_out), .Result(INST_Read[7]),
    .Carry_out(fulladder_7_carry_out));
  FullAdder fulladder_8 (
    .A(A[8]), .B(B[8]), .Carry_in(fulladder_7_carry_out), .Result(INST_Read[8]),
    .Carry_out(fulladder_8_carry_out));
  FullAdder fulladder_9 (
    .A(A[9]), .B(B[9]), .Carry_in(fulladder_8_carry_out), .Result(INST_Read[9]),
    .Carry_out(fulladder_9_carry_out));
  FullAdder fulladder_10 (
    .A(A[10]), .B(B[10]), .Carry_in(fulladder_9_carry_out), .Result(INST_Read[10]),
    .Carry_out(fulladder_10_carry_out));
  FullAdder fulladder_11 (
    .A(A[11]), .B(B[11]), .Carry_in(fulladder_10_carry_out), .Result(INST_Read[11]),
    .Carry_out(fulladder_11_carry_out));
  FullAdder fulladder_12 (
    .A(A[12]), .B(B[12]), .Carry_in(fulladder_11_carry_out), .Result(INST_Read[12]),
    .Carry_out(fulladder_12_carry_out));
  FullAdder fulladder_13 (
    .A(A[13]), .B(B[13]), .Carry_in(fulladder_12_carry_out), .Result(INST_Read[13]),
    .Carry_out(fulladder_13_carry_out));
  FullAdder fulladder_14 (
    .A(A[14]), .B(B[14]), .Carry_in(fulladder_13_carry_out), .Result(INST_Read[14]),
    .Carry_out(fulladder_14_carry_out));
  FullAdder fulladder_15 (
    .A(A[15]), .B(B[15]), .Carry_in(fulladder_14_carry_out), .Result(INST_Read[15]), .Carry_out(c_out));
endmodule

module ALU (
  input  enable,
  input  [15:0] Input_A,
  input  [15:0] Input_B,
  input  Operation,
  output [15:0] Result,
  output Carry_Out
);

  wire [15:0] and_1_out, multiplexer_1_out, multiplexer_2_out, multiplexer_3_out, n16bitadder_1_inst_read;

  Multiplexer #(.width(16)) multiplexer_1 (
    .in0({16{1'b0}}), .in1({16{1'b1}}), .out(multiplexer_1_out), .sel(enable));  // open: en
  Multiplexer #(.width(16)) multiplexer_2 (
    .in0({16{1'b0}}), .in1(Input_A), .out(multiplexer_2_out), .sel(enable));  // open: en
  Multiplexer #(.width(16)) multiplexer_3 (
    .in0({16{1'b0}}), .in1(Input_B), .out(multiplexer_3_out), .sel(enable));  // open: en
  assign and_1_out = Input_A & multiplexer_1_out & Input_B;  // AND_Gate and_1, 16 bits wide
  _16bitAdder u_16bitadder_1 (
    .c_out(Carry_Out), .A(multiplexer_2_out), .B(multiplexer_3_out), .INST_Read(n16bitadder_1_inst_read));
  Multiplexer #(.width(16)) multiplexer_4 (
    .in0(and_1_out), .in1(n16bitadder_1_inst_read), .out(Result), .sel(Operation));  // open: en
endmodule

module HalfAdder (
  input  A,
  input  B,
  output Sum,
  output carry_out
);

  xor xor_1 (Sum, A, B);
  and and_1 (carry_out, A, B);
endmodule

// State 4
module ControlUnit (
  input  [15:0] instruction,
  input  Clock,
  input  zf,
  input  cf,
  input  [15:0] OP1_Value,
  input  [15:0] OP2_Value,
  output PC_Read,
  output INST_Read,
  output ALUoperation,
  output IMMoperation,
  output dataMemRead_signal,
  output MemWrite_signal,
  output PCwrite_signal,
  output Pcselect_signal,
  output [2:0] out_15,
  output [2:0] out_16,
  output [2:0] out_17,
  output [2:0] out_18,
  output regWrite_signal,
  output [2:0] out_20,
  output [9:0] out_21,
  output [5:0] out_22,
  output [10:0] out_23,
  output ALUcontrol_signal,
  output zf_value,
  output [2:0] out_26,
  output [2:0] out_27,
  output cf_value,
  output CMP_signal,
  output flagWrite_signal
);

  wire ADD, ADDI, AND, and_1_out, and_2_out, and_4_out, and_5_out, and_6_out, and_7_out, and_8_out,
       and_9_out, and_10_out, ANDI, CMP, e, JA, JAE, JB, JBE, JE, JUMP, LD, multiplexer_1_out,
       multiplexer_2_out, multiplexer_3_out, n16bitcomparator_1_eq, n16bitcomparator_1_gt,
       n16bitcomparator_1_lt, nor_1_out, not_1_out, not_2_out, not_3_out, not_4_out, not_5_out, not_6_out,
       not_7_out, not_8_out, or_1_out, or_2_out, or_3_out, or_5_out, or_8_out, or_9_out, or_10_out,
       or_11_out, or_12_out, or_13_out, or_14_out, RESET, ST, State1, State3, State4, State5;
  wire [2:0] counter_1_q;

  assign out_21 = {{1{1'b0}}, instruction[8:0]};  // Bit_Extender bit_extender_1
  Decoder #(.select(4)) decoder_1 (
    .out0(AND), .out1(ADD), .out2(LD), .out3(ST), .out4(ANDI), .out5(ADDI), .out6(CMP), .out7(JUMP),
    .out8(JE), .out9(JA), .out10(JB), .out11(JBE), .out12(JAE), .sel(instruction[15:12]));  // open: out13, out14, out15, en
  or or_1 (or_1_out, AND, ADD, ANDI, ADDI);
  or or_2 (or_2_out, State3, State4);
  and and_1 (and_1_out, State4, or_1_out);
  or or_3 (or_3_out, State3, State4);
  and and_2 (and_2_out, or_3_out, LD);
  and and_3 (ALUcontrol_signal, or_1_out, or_2_out);
  or or_4 (regWrite_signal, and_1_out, and_2_out);
  or or_5 (or_5_out, JA, JE, JB, JAE, JBE, JUMP);
  not not_1 (not_1_out, or_5_out);
  Counter #(.width(3), .max('h4)) counter_1 (.Q(counter_1_q), .clk(Clock), .clr(RESET));  // open: load, D, count, carry
  and and_4 (and_4_out, or_5_out, State4);
  or or_6 (PC_Read, and_4_out, and_5_out);
  and and_5 (and_5_out, State1, not_1_out);
  Decoder #(.select(3), .enable("false")) decoder_2 (
    .out0(State1), .out1(INST_Read), .out2(State3), .out3(State4), .out4(State5), .sel(counter_1_q));  // open: out5, out6, out7
  nor nor_1 (nor_1_out, zf, cf);
  and and_6 (and_6_out, nor_1_out, JA);
  and and_7 (and_7_out, zf, JE, not_2_out);
  not not_2 (not_2_out, cf);
  not not_3 (not_3_out, zf);
  not not_4 (not_4_out, cf);
  and and_8 (and_8_out, zf, JB, not_3_out);
  and and_9 (and_9_out, not_4_out, JAE);
  and and_10 (and_10_out, cf, JBE, zf);
  and and_11 (CMP_signal, CMP, State3);
  and and_12 (flagWrite_signal, CMP, State4);
  _16BitComparator u_16bitcomparator_1 (
    .A(OP1_Value), .B(OP2_Value), .gt(n16bitcomparator_1_gt), .lt(n16bitcomparator_1_lt),
    .eq(n16bitcomparator_1_eq), .enable(e));
  or or_7 (e, CMP_signal, flagWrite_signal);
  or or_8 (or_8_out, State4, State3);
  or or_9 (or_9_out, JA, JE, JB, JAE, JBE, JUMP);
  or or_10 (or_10_out, and_6_out, and_7_out, and_8_out, and_9_out, and_10_out, JUMP);
  or or_11 (or_11_out, State3, State4);
  Multiplexer multiplexer_1 (.in0(1'b0), .in1(n16bitcomparator_1_gt), .out(multiplexer_1_out), .sel(e));  // open: en
  and and_13 (dataMemRead_signal, or_8_out, LD);
  and and_14 (Pcselect_signal, or_10_out, or_11_out);
  Multiplexer multiplexer_2 (.in0(1'b0), .in1(n16bitcomparator_1_lt), .out(multiplexer_2_out), .sel(e));  // open: en
  and and_15 (PCwrite_signal, or_9_out, State4);
  Multiplexer multiplexer_3 (.in0(1'b0), .in1(n16bitcomparator_1_eq), .out(multiplexer_3_out), .sel(e));  // open: en
  not not_5 (not_5_out, multiplexer_3_out);
  not not_6 (not_6_out, multiplexer_1_out);
  not not_7 (not_7_out, multiplexer_2_out);
  and and_16 (zf_value, multiplexer_3_out, not_7_out, not_8_out);
  not not_8 (not_8_out, multiplexer_1_out);
  and and_17 (cf_value, not_5_out, multiplexer_2_out, not_6_out);
  and and_18 (MemWrite_signal, State3, ST);
  or or_12 (or_12_out, JUMP, JE, JA, JBE, JAE, JB);
  or or_13 (or_13_out, ANDI, ADD, ADDI, AND, CMP, LD, ST);
  and and_19 (RESET, State5, or_14_out);
  or or_14 (or_14_out, or_13_out, or_12_out);

  assign ALUoperation = instruction[12];
  assign IMMoperation = instruction[14];
  assign out_15 = instruction[11:9];
  assign out_16 = instruction[8:6];
  assign out_17 = instruction[5:3];
  assign out_18 = {instruction[9], instruction[10], instruction[11]};
  assign out_20 = instruction[11:9];
  assign out_22 = instruction[5:0];
  assign out_23 = instruction[11:1];
  assign out_26 = instruction[11:9];
  assign out_27 = instruction[8:6];

  // Other names for the same wires on the sheet: address_ld_st[9:0] = out_21; IMM[5:0] = instruction[5:0];
  //   address_jump[10:0] = instruction[11:1]; dest[2:0] = instruction[11:9];
  //   ld_dst[2:0] = {instruction[9], instruction[10], instruction[11]}; OP1[2:0] = instruction[11:9];
  //   st_src[2:0] = instruction[11:9]; OP2[2:0] = instruction[8:6]; src1[2:0] = instruction[8:6];
  //   src2[2:0] = instruction[5:3]; State2 = INST_Read
endmodule

module PCReg (
  input  [10:0] jump_ADDRESS,
  input  PCselect,
  input  Enable,
  input  Clock,
  input  Clear,
  output [9:0] PC_address
);

  wire [10:0] adder_result, multiplexer_1_out;
  wire [10:10] register_1_q;

  Multiplexer #(.width(11)) multiplexer_1 (
    .in0(11'h1), .in1(jump_ADDRESS), .out(multiplexer_1_out), .sel(PCselect));  // open: en
  _11bitAdder u_11bitadder_1 (
    .INST_Read(adder_result), .A(multiplexer_1_out), .B({register_1_q[10], PC_address}));  // open: c_out
  Register #(.width(11), .trigger("falling")) register_1 (
    .D(adder_result), .en(Enable), .Q({register_1_q[10], PC_address}), .clk(Clock), .clr(Clear));
endmodule

module _11bitAdder (
  input  [10:0] A,
  input  [10:0] B,
  output [10:0] INST_Read,
  output c_out
);

  wire fulladder_1_carry_out, fulladder_2_carry_out, fulladder_3_carry_out, fulladder_4_carry_out,
       fulladder_5_carry_out, fulladder_6_carry_out, fulladder_7_carry_out, fulladder_8_carry_out,
       fulladder_9_carry_out, halfadder_1_carry_out;

  HalfAdder halfadder_1 (.A(B[0]), .B(A[0]), .Sum(INST_Read[0]), .carry_out(halfadder_1_carry_out));
  FullAdder fulladder_1 (
    .A(A[1]), .B(B[1]), .Carry_in(halfadder_1_carry_out), .Result(INST_Read[1]),
    .Carry_out(fulladder_1_carry_out));
  FullAdder fulladder_2 (
    .A(A[2]), .B(B[2]), .Carry_in(fulladder_1_carry_out), .Result(INST_Read[2]),
    .Carry_out(fulladder_2_carry_out));
  FullAdder fulladder_3 (
    .A(A[3]), .B(B[3]), .Carry_in(fulladder_2_carry_out), .Result(INST_Read[3]),
    .Carry_out(fulladder_3_carry_out));
  FullAdder fulladder_4 (
    .A(A[4]), .B(B[4]), .Carry_in(fulladder_3_carry_out), .Result(INST_Read[4]),
    .Carry_out(fulladder_4_carry_out));
  FullAdder fulladder_5 (
    .A(A[5]), .B(B[5]), .Carry_in(fulladder_4_carry_out), .Result(INST_Read[5]),
    .Carry_out(fulladder_5_carry_out));
  FullAdder fulladder_6 (
    .A(A[6]), .B(B[6]), .Carry_in(fulladder_5_carry_out), .Result(INST_Read[6]),
    .Carry_out(fulladder_6_carry_out));
  FullAdder fulladder_7 (
    .A(A[7]), .B(B[7]), .Carry_in(fulladder_6_carry_out), .Result(INST_Read[7]),
    .Carry_out(fulladder_7_carry_out));
  FullAdder fulladder_8 (
    .A(A[8]), .B(B[8]), .Carry_in(fulladder_7_carry_out), .Result(INST_Read[8]),
    .Carry_out(fulladder_8_carry_out));
  FullAdder fulladder_9 (
    .A(A[9]), .B(B[9]), .Carry_in(fulladder_8_carry_out), .Result(INST_Read[9]),
    .Carry_out(fulladder_9_carry_out));
  FullAdder fulladder_10 (
    .A(A[10]), .B(B[10]), .Carry_in(fulladder_9_carry_out), .Result(INST_Read[10]), .Carry_out(c_out));
endmodule

module CPU (
  input  clock,
  input  in_2,
  input  in_3,
  output [9:0] out_4
);

  wire ALUcontrol, ALUop, cf, CMPsignal, controlunit_1_cf_value, controlunit_1_flagwrite_signal,
       controlunit_1_zf_value, IMMop, INSTRead, MemRead, MemWrite, multiplexer_5_out, multiplexer_6_out,
       or_1_out, PCRead, PCselect_signal, PCwrite_signal, regWrite, zf;
  wire [2:0] DEST, multiplexer_1_out, multiplexer_2_out, multiplexer_3_out, OP1, OP2, SRC1, SRC2, st_src;
  wire [5:0] IMM;
  wire [9:0] MemAddress;
  wire [10:0] JUMP_ADDR;
  wire [15:0] ALUresult, bit_extender_1_out, Instruction, MemData, multiplexer_4_out, multiplexer_7_out,
       op1value, op2value, rom_1_data;

  PCReg pcreg_1 (
    .jump_ADDRESS(JUMP_ADDR), .PCselect(PCselect_signal), .PC_address(out_4), .Enable(PCRead), .Clock(clock),
    .Clear(in_3));
  or or_1 (or_1_out, MemRead, MemWrite);
  ROM #(.addrWidth(10), .dataWidth(16)) rom_1 (.addr(out_4), .data(rom_1_data));  // open: sel
  RAM #(.addrWidth(10), .dataWidth(16), .bus("separate")) ram_1 (
    .addr(MemAddress), .din(op1value), .data(MemData), .sel(or_1_out), .clk(clock), .ld(MemRead));  // open: str, clr
  Register #(.width(16)) Instruction_Register (.D(rom_1_data), .en(INSTRead), .Q(Instruction), .clk(clock), .clr(in_2));
  Multiplexer #(.width(3)) multiplexer_1 (.in0(SRC2), .in1(OP2), .out(multiplexer_1_out), .sel(CMPsignal));  // open: en
  Multiplexer #(.width(3), .enable("false")) multiplexer_2 (
    .in0(multiplexer_3_out), .in1(st_src), .out(multiplexer_2_out), .sel(MemWrite));
  Multiplexer #(.width(3)) multiplexer_3 (.in0(SRC1), .in1(OP1), .out(multiplexer_3_out), .sel(CMPsignal));  // open: en
  ControlUnit controlunit_1 (
    .instruction(Instruction), .Clock(clock), .PC_Read(PCRead), .INST_Read(INSTRead),
    .dataMemRead_signal(MemRead), .MemWrite_signal(MemWrite), .PCwrite_signal(PCwrite_signal),
    .Pcselect_signal(PCselect_signal), .out_15(DEST), .out_16(SRC1), .CMP_signal(CMPsignal), .out_17(SRC2),
    .regWrite_signal(regWrite), .out_20(st_src), .out_21(MemAddress),
    .flagWrite_signal(controlunit_1_flagwrite_signal), .out_22(IMM), .out_23(JUMP_ADDR),
    .ALUcontrol_signal(ALUcontrol), .out_26(OP1), .out_27(OP2), .OP1_Value(op1value), .OP2_Value(op2value),
    .ALUoperation(ALUop), .IMMoperation(IMMop), .zf_value(controlunit_1_zf_value),
    .cf_value(controlunit_1_cf_value), .zf(zf), .cf(cf));  // open: out_18
  RegisterFile registerfile_1 (
    .ReadRegister1(multiplexer_2_out), .ReadRegister2(multiplexer_1_out), .Write_Register(DEST),
    .Input(multiplexer_4_out), .RegisterWrite(regWrite), .Clock(clock), .ReadData1(op1value),
    .ReadData2(op2value));  // open: reset
  Multiplexer #(.width(16)) multiplexer_4 (
    .in0(ALUresult), .in1(MemData), .out(multiplexer_4_out), .sel(MemRead));  // open: en
  Multiplexer multiplexer_5 (
    .in0(cf), .in1(controlunit_1_cf_value), .out(multiplexer_5_out), .sel(controlunit_1_flagwrite_signal));  // open: en
  Multiplexer multiplexer_6 (
    .in0(zf), .in1(controlunit_1_zf_value), .out(multiplexer_6_out), .sel(controlunit_1_flagwrite_signal));  // open: en
  assign bit_extender_1_out = {{10{1'b0}}, IMM};  // Bit_Extender bit_extender_1
  Register #(.width(1)) u_CF (.D(multiplexer_5_out), .Q(cf), .clk(clock));  // open: en, clr
  Register #(.width(1)) u_ZF (.D(multiplexer_6_out), .Q(zf), .clk(clock));  // open: en, clr
  Multiplexer #(.width(16)) multiplexer_7 (
    .in0(op2value), .in1(bit_extender_1_out), .out(multiplexer_7_out), .sel(IMMop));  // open: en
  ALU alu_1 (
    .Input_A(op1value), .Input_B(multiplexer_7_out), .Operation(ALUop), .Result(ALUresult),
    .enable(ALUcontrol));  // open: Carry_Out

  // Other names for the same wires on the sheet: StoreValue[15:0] = op1value

  // Notes on the sheet:
  //   contents of rom_1 (hex, n*v repeats v):
  //   2400 5282 3264 3203 7008 0 0 0 7008 0 0 0 7008 0 0 2400 7ffe
endmodule
